// Digital circuit control.dig as structural Verilog
module control (
  input  [15:0] Instr,
  input  En,
  output [3:0] RT,
  output RTW,
  output [3:0] RA,
  output [3:0] AluOp,
  output AluD,
  output [7:0] Imm,
  output LoD,
  output HiD,
  output Jmp,
  output [3:0] JT,
  output Halt,
  output JReg,
  output RReg,
  output MemD,
  output RTD,
  output WMem,
  output WPC,
  output SPA,
  output MSP,
  output SPD,
  output DtoPC,
  output [1:0] PA,
  output PtoD,
  output PFtoD,
  output PW,
  output SPtoD,
  output SPSub,
  output SPL
);

  wire _0_3RA, _0_7Imm, _4_7RT, _4_15AllHigh, _8_11AluOp, _8_11Imm, _8_11JT, _8_11RT, _10_11PA, and_1_out,
       and_3_out, and_4_out, and_5_out, and_6_out, and_7_out, and_8_out, and_9_out, and_10_out, and_11_out,
       and_12_out, and_13_out, and_15_out, and_16_out, and_17_out, and_18_out, and_20_out, and_45_out,
       and_46_out, and_47_out, decoder_1_out_1, decoder_2_out_0, decoder_2_out_1, decoder_2_out_2,
       decoder_2_out_4, decoder_4_out_0, decoder_4_out_4, decoder_4_out_5, decoder_4_out_6, decoder_4_out_7,
       DtoPC_t, Halt_t, HiD_t, Jmp_t, JReg_t, LoD_t, MemD_t, MSP_t, or_1_out, or_2_out, or_4_out, or_7_out,
       or_8_out, or_15_out, PFtoD_t, PtoD_t, PW_t, RReg_t, RTD_t, RTW_t, SPA_t, SPD_t, SPL_t, SPSub_t,
       SPtoD_t, WMem_t, WPC_t;
  wire [1:0] PA_t;
  wire [3:0] AluOp_t, JT_t, multiplexer_1_out, RA_t, RT_t;
  wire [7:0] Imm_t;

  Decoder #(.Selector_Bits(4)) decoder_1 (
    .sel(Instr[11:8]), .out_1(decoder_1_out_1));  // open: out_0, out_2, out_3, out_4, out_5, out_6, out_7, out_8, out_9, out_10, out_11, out_12, out_13, out_14, out_15
  Decoder #(.Selector_Bits(4)) decoder_2 (
    .sel(Instr[3:0]), .out_0(decoder_2_out_0), .out_1(decoder_2_out_1), .out_2(decoder_2_out_2),
    .out_3(SPSub_t), .out_4(decoder_2_out_4));  // open: out_5, out_6, out_7, out_8, out_9, out_10, out_11, out_12, out_13, out_14, out_15
  or or_1 (or_1_out, decoder_2_out_0, decoder_2_out_1);
  or or_2 (or_2_out, decoder_2_out_0, decoder_2_out_1, decoder_2_out_2, SPSub_t);
  and and_1 (and_1_out, and_5_out, decoder_1_out_1);
  and and_2 (SPtoD_t, and_1_out, decoder_2_out_4);
  and and_3 (and_3_out, and_1_out, decoder_2_out_2);
  and and_4 (and_4_out, and_1_out, SPSub_t);
  and and_5 (and_5_out, ~Instr[12], ~Instr[13], ~Instr[14], ~Instr[15]);  // And
  and and_6 (and_6_out, and_1_out, decoder_2_out_4);
  and and_7 (and_7_out, and_1_out, decoder_2_out_0);
  and and_8 (and_8_out, and_1_out, decoder_2_out_1);
  or or_3 (SPL_t, and_3_out, and_4_out);
  or or_4 (or_4_out, and_6_out, and_8_out);
  and and_9 (and_9_out, ~Instr[8], ~Instr[9], ~Instr[10], ~Instr[11]);  // And
  and and_10 (and_10_out, or_1_out, and_1_out);
  and and_11 (and_11_out, ~Instr[4], ~Instr[5], ~Instr[6], ~Instr[7]);  // And
  and and_12 (and_12_out, and_1_out, or_2_out);
  and and_13 (and_13_out, and_11_out, and_9_out, and_5_out);
  Multiplexer #(.Bits(4)) multiplexer_1 (.sel(and_13_out), .in_0(4'b0000), .in_1(Instr[3:0]), .out(multiplexer_1_out));
  Decoder #(.Selector_Bits(4)) decoder_3 (
    .sel(multiplexer_1_out), .out_1(DtoPC_t));  // open: out_0, out_2, out_3, out_4, out_5, out_6, out_7, out_8, out_9, out_10, out_11, out_12, out_13, out_14, out_15
  assign PA_t = _10_11PA ? Instr[11:10] : 2'bz;  // Driver driver_1
  assign JT_t = _8_11JT ? Instr[11:8] : 4'bz;  // Driver driver_2
  assign AluOp_t = _8_11AluOp ? Instr[11:8] : 4'bz;  // Driver driver_3
  assign RT_t = _8_11RT ? Instr[11:8] : 4'bz;  // Driver driver_4
  assign Imm_t = _8_11Imm ? {4'b0000, Instr[11:8]} : 8'bz;  // Driver driver_5
  Decoder #(.Selector_Bits(4)) decoder_4 (
    .sel(Instr[15:12]), .out_0(decoder_4_out_0), .out_1(_8_11AluOp), .out_2(LoD_t), .out_3(HiD_t),
    .out_4(decoder_4_out_4), .out_5(decoder_4_out_5), .out_6(decoder_4_out_6), .out_7(decoder_4_out_7),
    .out_8(WPC_t), .out_9(_10_11PA));  // open: out_10, out_11, out_12, out_13, out_14, out_15
  or or_5 (_8_11RT, LoD_t, HiD_t);
  or or_6 (_4_7RT, _8_11AluOp, decoder_4_out_6, decoder_4_out_7, _10_11PA, and_1_out);
  or or_7 (or_7_out, _8_11AluOp, LoD_t, HiD_t, decoder_4_out_6, _10_11PA);
  or or_8 (or_8_out, _8_11AluOp, decoder_4_out_5, decoder_4_out_6, decoder_4_out_7, WPC_t);
  or or_9 (_0_7Imm, LoD_t, HiD_t, decoder_4_out_4, WPC_t);
  or or_10 (Jmp_t, decoder_4_out_4, decoder_4_out_5, WPC_t, DtoPC_t);
  or or_11 (_8_11JT, decoder_4_out_4, decoder_4_out_5);
  and and_14 (Halt_t, decoder_4_out_0, _4_15AllHigh);
  and and_15 (and_15_out, WPC_t, Instr[11]);
  and and_16 (and_16_out, decoder_4_out_5, Instr[4]);
  and and_17 (and_17_out, WPC_t, Instr[8]);
  or or_12 (_8_11Imm, decoder_4_out_6, decoder_4_out_7);
  or or_13 (MemD_t, decoder_4_out_6, DtoPC_t, and_8_out);
  or or_14 (WMem_t, decoder_4_out_7, WPC_t, and_7_out);
  or or_15 (or_15_out, WPC_t, DtoPC_t);
  or or_16 (SPA_t, WPC_t, DtoPC_t, and_10_out);
  or or_17 (MSP_t, WPC_t, and_12_out, DtoPC_t);
  or or_18 (SPD_t, DtoPC_t, and_8_out);
  and and_18 (and_18_out, _10_11PA, Instr[8]);
  and and_19 (PW_t, _10_11PA, ~Instr[8]);  // And
  assign RT_t = _4_7RT ? Instr[7:4] : 4'bz;  // Driver driver_6
  or or_19 (RTW_t, or_7_out, or_4_out);
  or or_20 (_0_3RA, or_8_out, _10_11PA);
  or or_21 (JReg_t, decoder_4_out_5, and_15_out, DtoPC_t);
  or or_22 (RReg_t, and_16_out, and_17_out);
  and and_20 (and_20_out, _10_11PA, ~Instr[8]);  // And
  or or_23 (RTD_t, decoder_4_out_7, and_7_out, and_20_out);
  assign JT_t = or_15_out ? 4'b1111 : 4'bz;  // Driver driver_7
  and and_21 (PFtoD_t, and_18_out, Instr[9]);
  and and_22 (PtoD_t, and_18_out, ~Instr[9]);  // And
  assign Imm_t = _0_7Imm ? Instr[7:0] : 8'bz;  // Driver driver_8
  assign RA_t = _0_3RA ? Instr[3:0] : 4'bz;  // Driver driver_9
  and and_23 (RTW, RTW_t, En);
  and and_24 (AluD, _8_11AluOp, En);
  and and_25 (LoD, LoD_t, En);
  and and_26 (HiD, HiD_t, En);
  and and_27 (Jmp, Jmp_t, En);
  and and_28 (Halt, Halt_t, En);
  and and_29 (JReg, JReg_t, En);
  and and_30 (RReg, RReg_t, En);
  and and_31 (MemD, MemD_t, En);
  and and_32 (RTD, RTD_t, En);
  and and_33 (WMem, WMem_t, En);
  and and_34 (WPC, WPC_t, En);
  and and_35 (SPA, SPA_t, En);
  and and_36 (MSP, MSP_t, En);
  and and_37 (SPD, SPD_t, En);
  and and_38 (DtoPC, DtoPC_t, En);
  and and_39 (PtoD, PtoD_t, En);
  and and_40 (PFtoD, PFtoD_t, En);
  and and_41 (PW, PW_t, En);
  and and_42 (SPtoD, SPtoD_t, En);
  and and_43 (SPSub, SPSub_t, En);
  and and_44 (SPL, SPL_t, En);
  and and_45 (and_45_out, Instr[11], Instr[10]);
  and and_46 (and_46_out, Instr[9], Instr[8], Instr[7], Instr[6], Instr[5]);
  and and_47 (and_47_out, Instr[4], Instr[3], Instr[2], Instr[1], Instr[0]);
  assign RT = En ? RT_t : 4'bz;  // Driver driver_10
  assign RA = En ? RA_t : 4'bz;  // Driver driver_11
  assign AluOp = En ? AluOp_t : 4'bz;  // Driver driver_12
  assign Imm = En ? Imm_t : 8'bz;  // Driver driver_13
  assign JT = En ? JT_t : 4'bz;  // Driver driver_14
  assign PA = En ? PA_t : 2'bz;  // Driver driver_15
  and and_48 (_4_15AllHigh, and_45_out, and_46_out, and_47_out);

  // Other names for the same wires on the sheet: AluD_t = _8_11AluOp; _0_3[3:0] = Instr[3:0]; b0 = Instr[0];
  //   b4 = Instr[4]; _8_11[3:0] = Instr[11:8]; b8 = Instr[8]; b9 = Instr[9]; b11 = Instr[11]

  // Notes on the sheet:
  //   RT: Address of target register
  //   RTW: Address of target register
  //   RA: Address of argument register
  //   AluOp: ALU operation to perform
  //   En: Enabled when on
  //   AluD: High when ALU result should be sent to data bus
  //   Imm: 8 bit immediate value
  //   LoD: Write target with low bits set to Imm to data
  //   HiD: Write target with high bits set to Imm to data
  //   Jmp: When high, jump if jump decider is true
  //   JT: Four bit jump type
  //   Halt: When high, write jump location to data bus
  //   JReg: Jump using register based jump
  //   RReg: When jumping with a register, use it as a relative value
  //   MemD: When high, write memroy data to the data bus
  //   RTD: When high, write target register data to the data bus
  //   WMem: When high, write data from the data bus to memory
  //   WPC: When high, send the PC to memory instead of the data bus
  //   SPA: When high, use the stack pointer as the RAM address intead of the computed address
  //   MSP: When high, modify the stack pointer
  //   SPD: When high, decrement and use a pre-decremented address
  //   DtoPC: When high, write the data bus to the jumpCalc register value instead of the argument register
  //   PA: Two bit peripheral address
  //   PtoD: When high, write data from the selected peripheral to data
  //   PFtoD: When high, write flags from the selected peripheral to data
  //   PW: When high, write data to the selected peripheral from data
  //   SPtoD: When high, write the value of SP to data
  //   SPSub: When high, subtract the value of register A from SP instead of adding it
  //   SPL: When high, use the modified value of the stack pointer instead of the incremented
  //   =0000\_0001\_XXXX\_XXXX (Single register ops)
  //   Noop
endmodule
