// Digital circuit hardware.dig as structural Verilog
module hardware (
  input  clk,
  input  in_2,
  input  in_3,
  input  [15:0] in_4,
  input  in_5,
  input  in_6
);

  wire AluD, and_1_out, and_2_out, DtoPC, Halt, HiD, Jmp, JReg, jumpdecider_1_djmp, LoD, MemD, MSP,
       not_1_out, paddr_1__0, paddr_1__1, paddr_1__2, paddr_1__3, paddr_2__0, paddr_2__1, paddr_2__2,
       paddr_2__3, PFtoD, Phase_out, PtoD, PW, RReg, rs_ff_1_nq, rs_ff_1_q, RTD, RTW, SPA, SPD, Un_Halt_out,
       WMem, WPC;
  wire [1:0] undriven;
  wire [3:0] alu_1_fl, AluOp, JT, RA, RT;
  wire [7:0] addrcalc_1_p1;
  wire [15:0] add_1_s, addrcalc_1_p2, addrcalc_1_p3, counterpreset_1_out, driver_1_out, eepromdualport_1_d,
       InstrReg_q, jumpcalc_1_npc, multiplexer_1_out, multiplexer_2_out, multiplexer_3_out,
       multiplexer_4_out, multiplexer_5_out, multiplexer_6_out, multiplexer_7_out, PC_out, pulldown_1_out,
       pulldown_2_out, pulldown_3_out, pulldown_4_out, pulldown_5_out, pulldown_6_out, ramdualport_1_d,
       Registers_da, sub_1_s;

  Button Un_Halt (.out(Un_Halt_out));
  RS_FF rs_ff_1 (.S(Halt), .C(clk), .R(Un_Halt_out), .Q(rs_ff_1_q), .nQ(rs_ff_1_nq));
  and and_1 (and_1_out, rs_ff_1_nq, clk);
  LED Halted (.in(rs_ff_1_q));
  LED Running (.in(and_1_out));
  // Probe Cycle on and_1_out
  Counter Phase (.en(1'b1), .C(and_1_out), .clr(1'b0), .out(Phase_out));  // open: ovf
  not not_1 (not_1_out, Phase_out);
  // Probe IEx on Phase_out
  and and_2 (and_2_out, MSP, Phase_out);
  CounterPreset #(.Bits(16)) counterpreset_1 (
    .en(and_2_out), .C(and_1_out), .dir(SPD), .in(in_4), .ld(in_5), .clr(in_6), .out(counterpreset_1_out));  // open: ovf
  Add #(.Bits(16)) add_1 (.a(counterpreset_1_out), .b(16'h8000), .c_i(1'b0), .s(add_1_s));  // open: c_o
  // Probe SP on add_1_s
  Sub #(.Bits(16)) sub_1 (.a(add_1_s), .b(16'h1), .c_i(1'b0), .s(sub_1_s));  // open: c_o
  Multiplexer #(.Bits(16)) multiplexer_1 (
    .sel(DtoPC), .in_0(addrcalc_1_p2), .in_1(driver_1_out), .out(multiplexer_1_out));
  jumpCalc jumpcalc_1 (
    .PC(PC_out), .Imm(addrcalc_1_p1), .Reg(multiplexer_1_out), .JReg(JReg), .RRel(RReg), .nPC(jumpcalc_1_npc));
  jumpDecider jumpdecider_1 (.Jmp(Jmp), .JT(JT), .Fl(alu_1_fl), .DJmp(jumpdecider_1_djmp));
  Multiplexer #(.Bits(16)) multiplexer_2 (.sel(SPD), .in_0(add_1_s), .in_1(sub_1_s), .out(multiplexer_2_out));
  // Probe Jmp on jumpdecider_1_djmp
  CounterPreset #(.Bits(16)) PC (
    .en(not_1_out), .C(and_1_out), .dir(in_2), .in(jumpcalc_1_npc), .ld(jumpdecider_1_djmp), .clr(in_3),
    .out(PC_out));  // open: ovf
  // addrCalc addrcalc_1: pin names not known; wires that end beside it: addrcalc_1_p1, addrcalc_1_p2, addrcalc_1_p3
  Multiplexer #(.Bits(16)) multiplexer_3 (
    .sel(SPA), .in_0(addrcalc_1_p3), .in_1(multiplexer_2_out), .out(multiplexer_3_out));
  // Probe PC on PC_out
  Multiplexer #(.Bits(16)) multiplexer_4 (
    .sel(Phase_out), .in_0(PC_out), .in_1(multiplexer_3_out), .out(multiplexer_4_out));
  Multiplexer #(.Bits(16)) multiplexer_5 (.sel(WPC), .in_0(driver_1_out), .in_1(PC_out), .out(multiplexer_5_out));
  RegisterFile #(.AddrBits(4), .Bits(16)) Registers (
    .Din(driver_1_out), .we(RTW), .Rw(RT), .C(and_1_out), .Ra(RT), .Rb(RA), .Da(Registers_da),
    .Db(addrcalc_1_p2));
  RAMDualPort #(.AddrBits(16), .isProgramMemory("true"), .Bits(16)) ramdualport_1 (
    .A(multiplexer_4_out), .Din(multiplexer_5_out), .str(WMem), .C(and_1_out), .ld(1'b1), .D(ramdualport_1_d));
  assign driver_1_out = RTD ? Registers_da : 16'bz;  // Driver driver_1
  assign driver_1_out = MemD ? ramdualport_1_d : 16'bz;  // Driver driver_2
  Register #(.Bits(16)) InstrReg (.D(ramdualport_1_d), .C(and_1_out), .en(not_1_out), .Q(InstrReg_q));
  alu alu_1 (
    .Op(AluOp), .TData(Registers_da), .AData(addrcalc_1_p2), .DO(AluD), .Clk(and_1_out),
    .RData(driver_1_out), .Fl(alu_1_fl));
  // Probe Instr on InstrReg_q
  control control_1 (
    .Instr(InstrReg_q), .En(Phase_out), .RT(RT), .RTW(RTW), .RA(RA), .AluOp(AluOp), .AluD(AluD),
    .Imm(addrcalc_1_p1), .LoD(LoD), .HiD(HiD), .Jmp(Jmp), .JT(JT), .Halt(Halt), .JReg(JReg), .RReg(RReg),
    .MemD(MemD), .RTD(RTD));
  overwriter overwriter_1 (.Data(addrcalc_1_p1), .Lo(LoD), .Hi(HiD), .Val(Registers_da), .ValU(driver_1_out));
  // Probe Imm on addrcalc_1_p1
  pAddr paddr_1 (.A(undriven), .En(PW), ._0(paddr_1__0), ._1(paddr_1__1), ._2(paddr_1__2), ._3(paddr_1__3));
  pAddr paddr_2 (.A(undriven), .En(PtoD), ._0(paddr_2__0), ._1(paddr_2__1), ._2(paddr_2__2), ._3(paddr_2__3));
  EEPROMDualPort #(.AddrBits(16), .Bits(16)) eepromdualport_1 (
    .A(addrcalc_1_p2), .Din(driver_1_out), .str(paddr_1__0), .C(and_1_out), .ld(paddr_2__0),
    .D(eepromdualport_1_d));
  Multiplexer #(.Selector_Bits(2), .Bits(16)) multiplexer_6 (
    .sel(undriven), .in_0(eepromdualport_1_d), .in_1(pulldown_1_out), .in_2(pulldown_3_out),
    .in_3(pulldown_5_out), .out(multiplexer_6_out));
  PullDown #(.Bits(16)) pulldown_1 (.out(pulldown_1_out));
  PullDown #(.Bits(16)) pulldown_2 (.out(pulldown_2_out));
  PullDown #(.Bits(16)) pulldown_3 (.out(pulldown_3_out));
  PullDown #(.Bits(16)) pulldown_4 (.out(pulldown_4_out));
  PullDown #(.Bits(16)) pulldown_5 (.out(pulldown_5_out));
  PullDown #(.Bits(16)) pulldown_6 (.out(pulldown_6_out));
  assign driver_1_out = PtoD ? multiplexer_6_out : 16'bz;  // Driver driver_3
  assign driver_1_out = PFtoD ? multiplexer_7_out : 16'bz;  // Driver driver_4
  Multiplexer #(.Selector_Bits(2), .Bits(16)) multiplexer_7 (
    .sel(undriven), .in_0(16'h1), .in_1(pulldown_2_out), .in_2(pulldown_4_out), .in_3(pulldown_6_out),
    .out(multiplexer_7_out));
  // Probe PA on undriven
  // Probe Data on driver_1_out
  // Probe fOCZN on alu_1_fl

  // Notes on the sheet:
  //   clk: Hz: 5000
  //   contents of eepromdualport_1 (hex, n*v repeats v):
  //   48,65,6c,6c,6f,20,57,6f,72,6c,64,21
endmodule
